# Fritzing sketch schaltplan (saved by Fritzing 0.9.10b)
circuit board: 8.46667cm x 5.64444cm
breadboards: 1

parts:
  MCU = WeMos D1 Mini
  DHT1 = DHT11 Humitidy and Temperature Sensor
  R1 = Resistor [tolerance=±5% power=0.25 resistance=10k package=THT]
  Part1 = Soil Moisture Sensor

nets (from the schematic view):
  3V3: MCU.3V3, DHT1.VDD, R1.Pin_0, Part1.VCC
  N1: MCU.A0, Part1.SIG
  N2: MCU.D1, DHT1.DATA, R1.Pin_1
  GND: MCU.G, DHT1.GND, Part1.GND

custom parts:
  DHT11 Humitidy and Temperature Sensor: DHT11 Humidity and Temperature Sensor
